# Fritzing sketch BranchesDiagram (saved by Fritzing 0.9.9b)
breadboards: 1

parts:
  Part1 = Arduino Nano (Rev3.0) (ICSP)
  VCC1 = 4 x AAA Battery Mount
  J1 = Basic Servo

nets:
  GND: Part1.GND, VCC1.-, J1.gnd
  N1: Part1.D9, J1.pulse
  N2: VCC1.+, J1.vcc
